// Logisim project 32-bit ALU.circ as structural Verilog: 1 circuit, main circuit ALU
module ALU (
  input  [31:0] B,
  input  [31:0] A,
  input  [4:0] in_3,
  output greater,
  output less_Flag,
  output Zero,
  output [31:0] result
);

  wire and_1_out, not_1_out;
  wire [31:0] M0, M1, M2, M3, M4;

  and and_1 (and_1_out, in_3[0], not_1_out);
  not not_1 (not_1_out, in_3[1]);
  _32_bit_Shift_Rotate u_32_bit_shift_rotate_1 (.shift_rotate_amount(B[4:0]), .A(A), .selector(in_3[1:0]), .result(M1));
  _32_bit_Arithmetic_Unit u_32_bit_arithmetic_unit_1 (
    .A(A), .B(B), .result(M2), .Sub(and_1_out), .Less(M3), .great(greater), .equal(M4), .Zero_flag(Zero),
    .less_FLag(less_Flag));  // open: Overflow_flag
  _32_bit_logic_unit u_32_bit_logic_unit_1 (.A(A), .B(B), .out_4(M0), .in_3(in_3[1:0]));
  Multiplexer #(.select(3), .width(32), .enable("false")) multiplexer_1 (
    .in0(M0), .in1(M1), .in2(M2), .in3(M3), .in4(M4), .out(result), .sel(in_3[4:2]));  // open: in5, in6, in7

  // Other names for the same wires on the sheet: _2 = in_3[2]; _3 = in_3[3]; _4 = in_3[4]; _0 = in_3[0]; _1 = in_3[1];
  //   shift_rotate_amount[4:0] = B[4:0]
endmodule
