// Logisim project 32-bit Logic Unit.circ as structural Verilog: 4 circuits, main circuit 32-bit AND
module _32_bit_AND (
  input  [31:0] A,
  input  [31:0] B,
  output [31:0] out_3
);

  and and_1 (out_3[0], A[0], B[0]);
  and and_2 (out_3[1], A[1], B[1]);
  and and_3 (out_3[2], A[2], B[2]);
  and and_4 (out_3[3], A[3], B[3]);
  and and_5 (out_3[4], A[4], B[4]);
  and and_6 (out_3[5], A[5], B[5]);
  and and_7 (out_3[6], A[6], B[6]);
  and and_8 (out_3[7], A[7], B[7]);
  and and_9 (out_3[8], A[8], B[8]);
  and and_10 (out_3[9], A[9], B[9]);
  and and_11 (out_3[10], A[10], B[10]);
  and and_12 (out_3[11], A[11], B[11]);
  and and_13 (out_3[12], A[12], B[12]);
  and and_14 (out_3[13], A[13], B[13]);
  and and_15 (out_3[14], A[14], B[14]);
  and and_16 (out_3[15], A[15], B[15]);
  and and_17 (out_3[16], A[16], B[16]);
  and and_18 (out_3[17], A[17], B[17]);
  and and_19 (out_3[18], A[18], B[18]);
  and and_20 (out_3[19], A[19], B[19]);
  and and_21 (out_3[20], A[20], B[20]);
  and and_22 (out_3[21], A[21], B[21]);
  and and_23 (out_3[22], A[22], B[22]);
  and and_24 (out_3[23], A[23], B[23]);
  and and_25 (out_3[24], A[24], B[24]);
  and and_26 (out_3[25], A[25], B[25]);
  and and_27 (out_3[26], A[26], B[26]);
  and and_28 (out_3[27], A[27], B[27]);
  and and_29 (out_3[28], A[28], B[28]);
  and and_30 (out_3[29], A[29], B[29]);
  and and_31 (out_3[30], A[30], B[30]);
  and and_32 (out_3[31], A[31], B[31]);
endmodule

module _32_bit_logic_unit (
  input  [31:0] A,
  input  [31:0] B,
  input  [1:0] in_3,
  output [31:0] out_4
);

  wire [31:0] n32_bit_and_1_out_3, n32_bit_or_1_out_3, n32_bit_xor_1_out_3, n32_bit_xor_2_out_3, not_1_out;

  assign not_1_out = ~A;  // NOT_Gate not_1, 32 bits wide
  _32_bit_AND u_32_bit_and_1 (.A(A), .B(B), .out_3(n32_bit_and_1_out_3));
  _32_bit_OR u_32_bit_or_1 (.A(A), .B(B), .out_3(n32_bit_or_1_out_3));
  _32_bit_XOR u_32_bit_xor_1 (.A(A), .B(B), .out_3(n32_bit_xor_1_out_3));
  _32_bit_XOR u_32_bit_xor_2 (.A(not_1_out), .B(B), .out_3(n32_bit_xor_2_out_3));
  Multiplexer #(.select(2), .width(32), .enable("false")) multiplexer_1 (
    .in0(n32_bit_and_1_out_3), .in1(n32_bit_or_1_out_3), .in2(n32_bit_xor_1_out_3),
    .in3(n32_bit_xor_2_out_3), .out(out_4), .sel(in_3));
endmodule

module _32_bit_OR (
  input  [31:0] A,
  input  [31:0] B,
  output [31:0] out_3
);

  or or_1 (out_3[0], A[0], B[0]);
  or or_2 (out_3[1], A[1], B[1]);
  or or_3 (out_3[2], A[2], B[2]);
  or or_4 (out_3[3], A[3], B[3]);
  or or_5 (out_3[4], A[4], B[4]);
  or or_6 (out_3[5], A[5], B[5]);
  or or_7 (out_3[6], A[6], B[6]);
  or or_8 (out_3[7], A[7], B[7]);
  or or_9 (out_3[8], A[8], B[8]);
  or or_10 (out_3[9], A[9], B[9]);
  or or_11 (out_3[10], A[10], B[10]);
  or or_12 (out_3[11], A[11], B[11]);
  or or_13 (out_3[12], A[12], B[12]);
  or or_14 (out_3[13], A[13], B[13]);
  or or_15 (out_3[14], A[14], B[14]);
  or or_16 (out_3[15], A[15], B[15]);
  or or_17 (out_3[16], A[16], B[16]);
  or or_18 (out_3[17], A[17], B[17]);
  or or_19 (out_3[18], A[18], B[18]);
  or or_20 (out_3[19], A[19], B[19]);
  or or_21 (out_3[20], A[20], B[20]);
  or or_22 (out_3[21], A[21], B[21]);
  or or_23 (out_3[22], A[22], B[22]);
  or or_24 (out_3[23], A[23], B[23]);
  or or_25 (out_3[24], A[24], B[24]);
  or or_26 (out_3[25], A[25], B[25]);
  or or_27 (out_3[26], A[26], B[26]);
  or or_28 (out_3[27], A[27], B[27]);
  or or_29 (out_3[28], A[28], B[28]);
  or or_30 (out_3[29], A[29], B[29]);
  or or_31 (out_3[30], A[30], B[30]);
  or or_32 (out_3[31], A[31], B[31]);
endmodule

module _32_bit_XOR (
  input  [31:0] A,
  input  [31:0] B,
  output [31:0] out_3
);

  xor xor_1 (out_3[0], A[0], B[0]);
  xor xor_2 (out_3[1], A[1], B[1]);
  xor xor_3 (out_3[2], A[2], B[2]);
  xor xor_4 (out_3[3], A[3], B[3]);
  xor xor_5 (out_3[4], A[4], B[4]);
  xor xor_6 (out_3[5], A[5], B[5]);
  xor xor_7 (out_3[6], A[6], B[6]);
  xor xor_8 (out_3[7], A[7], B[7]);
  xor xor_9 (out_3[8], A[8], B[8]);
  xor xor_10 (out_3[9], A[9], B[9]);
  xor xor_11 (out_3[10], A[10], B[10]);
  xor xor_12 (out_3[11], A[11], B[11]);
  xor xor_13 (out_3[12], A[12], B[12]);
  xor xor_14 (out_3[13], A[13], B[13]);
  xor xor_15 (out_3[14], A[14], B[14]);
  xor xor_16 (out_3[15], A[15], B[15]);
  xor xor_17 (out_3[16], A[16], B[16]);
  xor xor_18 (out_3[17], A[17], B[17]);
  xor xor_19 (out_3[18], A[18], B[18]);
  xor xor_20 (out_3[19], A[19], B[19]);
  xor xor_21 (out_3[20], A[20], B[20]);
  xor xor_22 (out_3[21], A[21], B[21]);
  xor xor_23 (out_3[22], A[22], B[22]);
  xor xor_24 (out_3[23], A[23], B[23]);
  xor xor_25 (out_3[24], A[24], B[24]);
  xor xor_26 (out_3[25], A[25], B[25]);
  xor xor_27 (out_3[26], A[26], B[26]);
  xor xor_28 (out_3[27], A[27], B[27]);
  xor xor_29 (out_3[28], A[28], B[28]);
  xor xor_30 (out_3[29], A[29], B[29]);
  xor xor_31 (out_3[30], A[30], B[30]);
  xor xor_32 (out_3[31], A[31], B[31]);
endmodule
