// Logisim project 32-bit Shifting and Rotating unit.circ as structural Verilog: 1 circuit, main circuit 32-bit Shift/Rotate
module _32_bit_Shift_Rotate (
  input  [4:0] shift_rotate_amount,
  input  [31:0] A,
  input  [1:0] selector,
  output [31:0] result
);

  wire [4:0] s_r;
  wire [31:0] shifter_1_out, shifter_2_out, shifter_3_out;

  Shifter #(.width(32)) shifter_1 (.in(A), .\dist (s_r), .out(shifter_1_out));
  Shifter #(.width(32), .shift("lr")) shifter_2 (.in(A), .\dist (s_r), .out(shifter_2_out));
  Shifter #(.width(32), .shift("rr")) shifter_3 (.in(A), .\dist (s_r), .out(shifter_3_out));
  Multiplexer #(.select(2), .width(32)) multiplexer_1 (
    .in0(shifter_1_out), .in1(shifter_2_out), .in2(shifter_3_out), .out(result), .sel(selector));  // open: in3, en

  // Other names for the same wires on the sheet: s_r_t[4:0] = shift_rotate_amount
endmodule
