// Logisim project CPU.circ as structural Verilog: 2 circuits, main circuit piple line CPU
module piple_line_CPU (
  input  in_1,
  input  clear,
  output [19:0] out_3,
  output [1:0] out_4,
  output [19:0] out_5,
  output [10:0] out_6,
  output [1:0] out_7,
  output [31:0] out_8,
  output [31:0] out_9,
  output [31:0] out_10,
  output [1:0] out_11,
  output [31:0] out_12,
  output [31:0] out_13,
  output [31:0] out_14,
  output [1:0] out_15,
  output [31:0] out_16,
  output [2:0] out_17,
  output [19:0] out_18,
  output [31:0] out_19,
  output [31:0] out_20,
  output [1:0] out_21,
  output [2:0] out_22,
  output [31:0] out_23,
  output [1:0] out_24,
  output [1:0] out_25,
  output [31:0] out_26,
  output [2:0] out_27,
  output [31:0] out_28,
  output [31:0] out_29,
  output [1:0] out_30,
  output [4:0] out_31,
  output [15:0] out_32,
  output [4:0] out_33
);

  wire ALuSrc, ALuSrc_EX, B, B_EX, B_ID, BEQ, BEQ_ID, BNE, BNE_ID, Branch_taken, CLK, comparator_1_eq,
       control_mux, equal_ID, great, great_ID, I_type_Hazard, IF_write, J, J_ID, JAL, JAL_MEM, JAL_WB, JR,
       JR_ID, less, less_ID, MemRead, MemRead_MEM, MemTOReg, MemTOReg_MEM, MemWrite, MemWrite_MEM, not_1_out,
       not_3_out, PC_write, RegDist, RegDist_EX, RegDist_ID, SSET, SSET_EX, TE, TE_ID, WR, WR_MEM, WR_WB,
       zeroFlag;
  wire [1:0] ALU_O_P, ALU_O_P_ID, extendType, ImmedaiteType, R0;
  wire [2:0] _3_bit_Rd, _3_bit_Rd_EX, _3_bit_Rd_ID, _3_bit_Rd_MEM, _3_bit_Rd_WB, _3_bit_Rs, _3_bit_Rs_EX,
       _3_bit_Rt, _3_bit_Rt_EX, _3_bit_Rt_ID, multiplexer_11_out, multiplexer_12_out, multiplexer_16_out;
  wire [4:0] _5_bit_imm, ALUOp_EX, ID_TO__EX, multiplexer_24_out;
  wire [6:0] multiplexer_3_out;
  wire [7:0] _8_bit_imm;
  wire [14:0] IF_TO__ID;
  wire [19:0] adder_1_out, adder_2_out, adder_3_out, multiplexer_1_out, multiplexer_2_out, multiplexer_6_out,
       PC_ID;
  wire [24:0] multiplexer_7_out;
  wire [31:0] ALuResult_MEM, eight_32_bit_register_file_1_read_data1,
       eight_32_bit_register_file_1_read_data2, extImm_EX, multiplexer_4_out, multiplexer_5_out,
       multiplexer_14_out, multiplexer_19_out, multiplexer_22_out, multiplexer_23_out, pc_Extended,
       pc_Extended_EX, pc_Extended_ID, pc_Extended_MEM, pc_Extended_WB, ram_1_data, RdSh, ReadData1_EX,
       register_7_q, register_8_q;

  Adder #(.width(20)) adder_1 (.a(out_3), .b(20'h2), .out(adder_1_out));  // open: cin, cout
  not not_1 (not_1_out, Branch_taken);
  Multiplexer #(.width(20), .enable("false")) multiplexer_1 (
    .in0(out_5), .in1(adder_1_out), .out(multiplexer_1_out), .sel(not_1_out));
  control_unit control_unit_1 (
    .MemToReg(MemTOReg), .MemRead(MemRead), .MemWrite(MemWrite), .WR(WR), .ALU_SRC(ALuSrc),
    .RegDist(RegDist), .SSEt(SSET), .TE(TE), .J(J), .JAL(JAL), .BEQ(BEQ), .BNE(BNE), .B(B),
    .ALU_o_p(ALU_O_P), .extender(extendType), .R0(R0), .OpCode(out_31), .ALU_function(out_33), .Jr(JR),
    .immediate(ImmedaiteType), .R_type_function(out_30), .I_type_Hazard(I_type_Hazard));
  Adder #(.width(20)) adder_2 (.a(PC_ID), .b(20'h2), .out(adder_2_out));  // open: cin, cout
  Multiplexer #(.width(20), .enable("false")) multiplexer_2 (
    .in0(multiplexer_1_out), .in1(out_3), .out(multiplexer_2_out), .sel(PC_write));
  Comparator #(.width(20)) comparator_1 (.a(out_5), .b(adder_2_out), .eq(comparator_1_eq));  // open: gt, lt
  Register #(.width(20), .trigger("falling")) PC (.D(multiplexer_2_out), .Q(out_3), .clk(CLK), .clr(in_1));  // open: en
  not not_2 (Branch_taken, comparator_1_eq);
  Instruction_Memory instruction_memory_1 (
    .PC(out_3), ._11_bit_immediate(out_32[10:0]), ._8_bit_immediate(_8_bit_imm),
    ._5_bit_immediate(_5_bit_imm), ._5_bit_OpCode(out_31), ._3_bit_Rd(_3_bit_Rd), ._3_bit_Rs(_3_bit_Rs),
    ._3_bit_Rt(_3_bit_Rt), ._2_bit_R_Func(out_30), .Clear(clear));
  Multiplexer #(.width(7), .enable("false")) multiplexer_3 (
    .in0({JR, ALU_O_P, BNE, BEQ, J, TE}), .in1({7{1'b0}}), .out(multiplexer_3_out), .sel(Branch_taken));
  Multiplexer #(.width(32), .enable("false")) multiplexer_4 (
    .in0(out_8), .in1({32{1'b0}}), .out(multiplexer_4_out), .sel(Branch_taken));
  Multiplexer #(.width(32), .enable("false")) multiplexer_5 (
    .in0(pc_Extended), .in1({32{1'b0}}), .out(multiplexer_5_out), .sel(Branch_taken));
  Multiplexer #(.width(20), .enable("false")) multiplexer_6 (
    .in0(out_3), .in1({20{1'b0}}), .out(multiplexer_6_out), .sel(Branch_taken));
  Multiplexer #(.width(25), .enable("false")) multiplexer_7 (
    .in0({WR, JAL, MemTOReg, MemWrite, MemRead, R0, B, SSET, ALuSrc, out_33, RegDist, _3_bit_Rt, _3_bit_Rs, _3_bit_Rd}),
    .in1({25{1'b0}}), .out(multiplexer_7_out), .sel(Branch_taken));
  PC_Programming pc_programming_1 (
    .PC(PC_ID), .IMM(out_6), .BNE(BNE_ID), .B(B_ID), .BEQ(BEQ_ID), .JR(JR_ID), .J(J_ID), .JAL(IF_TO__ID[13]),
    .RD(out_26), .greater(great_ID), .less(less_ID), .zeroFlag(equal_ID), .in_8(ALU_O_P_ID), .TE(TE_ID),
    .result(out_5));
  Register #(.width(7), .trigger("falling")) register_1 (
    .D(multiplexer_3_out), .Q({JR_ID, ALU_O_P_ID, BNE_ID, BEQ_ID, J_ID, TE_ID}), .clk(CLK));  // open: en, clr
  Register #(.width(32), .trigger("falling")) register_2 (
    .D(multiplexer_4_out), .Q({out_10[31:11], out_6}), .clk(CLK));  // open: en, clr
  Register #(.width(32), .trigger("falling")) register_3 (
    .D(multiplexer_5_out), .Q(pc_Extended_ID), .clk(CLK));  // open: en, clr
  Register #(.width(20), .trigger("falling")) register_4 (
    .D(multiplexer_6_out), .Q(PC_ID), .clk(CLK));  // open: en, clr
  Register #(.width(25), .trigger("falling")) register_5 (
    .D(multiplexer_7_out),
    .Q({IF_TO__ID[14:8], B_ID, IF_TO__ID[6:0], RegDist_ID, _3_bit_Rt_ID, out_17, _3_bit_Rd_ID}), .clk(CLK));  // open: en, clr
  Adder #(.width(20)) adder_3 (.a(out_3), .b(20'h2), .out(adder_3_out));  // open: cin, cout
  Extender extender_1 (
    .in_3(out_32[10:0]), .in_4(_8_bit_imm), .in_5(_5_bit_imm), .extend_input(extendType),
    .immediate(ImmedaiteType), .extended_immediate(out_8));
  Multiplexer #(.width(3), .enable("false")) multiplexer_8 (
    .in0(_3_bit_Rt_ID), .in1(_3_bit_Rd_ID), .out(out_22), .sel(RegDist_ID));
  Multiplexer #(.width(3), .enable("false")) multiplexer_9 (
    .in0(_3_bit_Rd_WB), .in1(3'b111), .out(out_27), .sel(JAL_WB));
  Multiplexer #(.width(32), .enable("false")) multiplexer_10 (
    .in0(out_23), .in1(pc_Extended_WB), .out(out_29), .sel(JAL_WB));
  Forward_unit__Branch forward_unit_branch_1 (
    .RD_WR(_3_bit_Rd_WB), .RD_MEM(_3_bit_Rd_MEM), .RD_EX(_3_bit_Rd_EX), .RD_ID(_3_bit_Rd_ID), .RS_ID(out_17),
    .forward_D(out_4), .forward_S(out_7), .BEQ(BEQ_ID), .B(B_ID), .BNE(BNE_ID));
  Clock clock_1 (.out(CLK));
  _20_32_bit_Extender u_20_32_bit_extender_1 (.Imm(adder_3_out), .in_2(1'b0), .out_3(pc_Extended));
  eight_32_bit_register_file eight_32_bit_register_file_1 (
    .Read_Register1(out_17), .Read_Register2(out_22), .Write_Register(out_27), .Write_Data(out_29),
    .Read_Data1(eight_32_bit_register_file_1_read_data1),
    .Read_Data2(eight_32_bit_register_file_1_read_data2), .RegWrite(WR_WB), .clock(CLK));
  Multiplexer #(.width(3), .enable("false")) multiplexer_11 (
    .in0(_3_bit_Rd_WB), .in1(3'b111), .out(multiplexer_11_out), .sel(JAL_WB));
  Multiplexer #(.width(3), .enable("false")) multiplexer_12 (
    .in0(_3_bit_Rd_MEM), .in1(3'b111), .out(multiplexer_12_out), .sel(JAL_WB));
  Comparator #(.width(32)) comparator_2 (.a(out_26), .b(out_12), .gt(great_ID), .eq(equal_ID), .lt(less_ID));
  Multiplexer #(.width(32), .enable("false")) multiplexer_13 (
    .in0(multiplexer_14_out), .in1({32{1'b0}}), .out(out_12), .sel(B_ID));
  Multiplexer #(.select(2), .width(32), .enable("false")) multiplexer_14 (
    .in0(eight_32_bit_register_file_1_read_data1), .in1(out_29), .in2(out_9), .in3(out_20),
    .out(multiplexer_14_out), .sel(out_7));
  Multiplexer #(.select(2), .width(32), .enable("false")) multiplexer_15 (
    .in0(eight_32_bit_register_file_1_read_data2), .in1(out_29), .in2(out_9), .in3(out_20), .out(out_26),
    .sel(out_4));
  Multiplexer #(.width(3), .enable("false")) multiplexer_16 (
    .in0(_3_bit_Rt_EX), .in1(_3_bit_Rd_EX), .out(multiplexer_16_out), .sel(RegDist_EX));
  Forwarding_Unit forwarding_unit_1 (
    .EX_MEM_Rd(multiplexer_12_out), .ID_EX_Rs(_3_bit_Rs_EX), .MEM_WB_Rd(multiplexer_11_out),
    .ID_EX_Rt(multiplexer_16_out), .Forwarding_A(out_11), .Forwarding_B(out_21), .MEM_WB_WR(WR_WB),
    .EX_MEM_WR(WR_MEM));
  Register #(.width(6), .trigger("falling")) register_6 (
    .D({out_17, _3_bit_Rt_ID}), .Q({_3_bit_Rs_EX, _3_bit_Rt_EX}), .clk(CLK));  // open: en, clr
  Register #(.width(32), .trigger("falling")) register_7 (.D(out_12), .Q(register_7_q), .clk(CLK));  // open: en, clr
  Register #(.width(32), .trigger("falling")) register_8 (.D(out_26), .Q(register_8_q), .clk(CLK));  // open: en, clr
  Register #(.width(32), .trigger("falling")) register_9 (
    .D({out_10[31:11], out_6}), .Q(extImm_EX), .clk(CLK));  // open: en, clr
  Register #(.width(32), .trigger("falling")) register_10 (
    .D(pc_Extended_ID), .Q(pc_Extended_EX), .clk(CLK));  // open: en, clr
  Register #(.width(19), .trigger("falling")) register_11 (
    .D({RegDist_ID, IF_TO__ID[14:8], B_ID, IF_TO__ID[6:0], _3_bit_Rd_ID}),
    .Q({RegDist_EX, ID_TO__EX, out_24, B_EX, SSET_EX, ALuSrc_EX, ALUOp_EX, _3_bit_Rd_EX}), .clk(CLK));  // open: en, clr
  Multiplexer #(.select(2), .width(32), .enable("false")) multiplexer_17 (
    .in0(register_7_q), .in1(out_9), .in2(out_23), .out(ReadData1_EX), .sel(out_11));  // open: in3
  Multiplexer #(.select(2), .width(32), .enable("false")) multiplexer_18 (
    .in0(register_8_q), .in1(out_9), .in2(out_23), .out(out_13), .sel(out_21));  // open: in3
  Hazard_detection_unit hazard_detection_unit_1 (
    .ID_EX_MemRead(ID_TO__EX[1]), .IF_ID_Rs(out_17), .IF_ID_Rt(_3_bit_Rt_ID), .ID_Ex_Rd(_3_bit_Rd_EX),
    .out_10(IF_write), .out_11(PC_write), .out_12(control_mux), .IF_ID_Rd(_3_bit_Rd_ID), .B(B_ID),
    .SSET(IF_TO__ID[6]), .I_type_Hazard(I_type_Hazard), .J(J_ID));
  Shifter #(.width(32)) shifter_1 (.in(out_13), .\dist (5'b01000), .out(RdSh));
  Multiplexer #(.width(32), .enable("false")) multiplexer_19 (
    .in0(out_13), .in1(RdSh), .out(multiplexer_19_out), .sel(SSET_EX));
  Multiplexer #(.select(2), .width(32), .enable("false")) multiplexer_20 (
    .in0(ReadData1_EX), .in1({32{1'b0}}), .in2(extImm_EX), .out(out_19), .sel(out_24));  // open: in3
  Multiplexer #(.width(32), .enable("false")) multiplexer_21 (
    .in0(multiplexer_19_out), .in1(extImm_EX), .out(out_28), .sel(ALuSrc_EX));
  Multiplexer #(.width(32), .enable("false")) multiplexer_22 (
    .in0(out_19), .in1(out_28), .out(multiplexer_22_out), .sel(B_EX));
  Multiplexer #(.width(32), .enable("false")) multiplexer_23 (
    .in0(out_28), .in1(out_19), .out(multiplexer_23_out), .sel(B_EX));
  ALU alu_1 (
    .B(multiplexer_23_out), .A(multiplexer_22_out), .greater(great), .less_Flag(less), .Zero(zeroFlag),
    .result(out_20), .in_3(ALUOp_EX));
  Multiplexer #(.width(5), .enable("false")) multiplexer_24 (
    .in0(ID_TO__EX), .in1({5{1'b0}}), .out(multiplexer_24_out), .sel(control_mux));
  Register #(.width(32), .trigger("falling")) register_12 (
    .D(pc_Extended_EX), .Q(pc_Extended_MEM), .clk(CLK));  // open: en, clr
  Register #(.width(32), .trigger("falling")) register_13 (.D(out_13), .Q(out_16), .clk(CLK));  // open: en, clr
  Register #(.width(32), .trigger("falling")) register_14 (.D(out_20), .Q(ALuResult_MEM), .clk(CLK));  // open: en, clr
  Register #(.trigger("falling")) register_15 (
    .D({multiplexer_24_out, _3_bit_Rd_EX}),
    .Q({WR_MEM, JAL_MEM, MemTOReg_MEM, MemWrite_MEM, MemRead_MEM, _3_bit_Rd_MEM}), .clk(CLK));  // open: en, clr
  not not_3 (not_3_out, CLK);
  Shifter #(.width(20)) shifter_2 (.in(ALuResult_MEM[19:0]), .\dist (5'b00010), .out(out_18));
  RAM #(.addrWidth(20), .dataWidth(32), .bus("separate")) ram_1 (
    .addr(out_18), .din(out_16), .data(ram_1_data), .str(MemWrite_MEM), .clk(not_3_out), .ld(MemRead_MEM));  // open: sel, clr
  Multiplexer #(.width(32), .enable("false")) multiplexer_25 (
    .in0(ALuResult_MEM), .in1(ram_1_data), .out(out_9), .sel(MemTOReg_MEM));
  Register #(.width(32), .trigger("falling")) register_16 (
    .D(pc_Extended_MEM), .Q(pc_Extended_WB), .clk(CLK));  // open: en, clr
  Register #(.width(32), .trigger("falling")) register_17 (.D(out_9), .Q(out_23), .clk(CLK));  // open: en, clr
  Register #(.width(5), .trigger("falling")) register_18 (
    .D({WR_MEM, JAL_MEM, _3_bit_Rd_MEM}), .Q({WR_WB, JAL_WB, _3_bit_Rd_WB}), .clk(CLK));  // open: en, clr

  assign out_10[10:0] = out_6;
  assign out_14 = out_9;
  assign out_15 = out_7;
  assign out_25 = out_4;
  assign out_32[15:11] = out_31;

  // Other names for the same wires on the sheet: _3_bit_Rs_ID[2:0] = out_17; _2_bit_Func[1:0] = out_30;
  //   _20_bit_AluResult[19:0] = out_18; ALUOp[4:0] = out_33; ALuResult_EX[31:0] = out_20; extImm[31:0] = out_8;
  //   Forward_D[1:0] = out_4; Forward_S[1:0] = out_7; Forwarding_A[1:0] = out_11; Forwarding_B[1:0] = out_21;
  //   _11_bit_Imm_ID[10:0] = out_6; ID_extImm[31:0] = {out_10[31:11], out_6}; MEM_read_EX = ID_TO__EX[1];
  //   SSET_ID = IF_TO__ID[6]; IF_TO__ID[7] = B_ID; JAL_ID = IF_TO__ID[13]; MEM_ALU[31:0] = out_9;
  //   MEM_ALU_WB[31:0] = out_23; _11_bit_imm[10:0] = out_32[10:0]; _5_bit_OpCode[4:0] = out_31; PC[19:0] = out_3;
  //   R0_EX[1:0] = out_24; ReadData1[31:0] = out_12; ReadData2[31:0] = out_26; ReadData2_EX[31:0] = out_13;
  //   ReadData2_MEM[31:0] = out_16; WRBD[31:0] = out_29
endmodule

module trash (
);

  wire [1:0] and_1_out, Forwarding_B;
  wire [1:1] ID_TO__EX;
  wire [31:0] MEM_ALU, MEM_ALU_WB, multiplexer_1_out, ReadData2_EX;

  Multiplexer #(.select(2), .width(32), .enable("false")) multiplexer_1 (
    .in0(ReadData2_EX), .in1(MEM_ALU), .in2(MEM_ALU_WB), .out(multiplexer_1_out), .sel(and_1_out));  // open: in3
  assign and_1_out = Forwarding_B & {2{ID_TO__EX[1]}};  // AND_Gate and_1, 2 bits wide
endmodule
