// Logisim project Control Unit.circ as structural Verilog: 2 circuits, main circuit control unit
module control_unit (
  input  [4:0] OpCode,
  input  [1:0] R_type_function,
  output MemToReg,
  output MemRead,
  output MemWrite,
  output ALU_SRC,
  output WR,
  output RegDist,
  output SSEt,
  output TE,
  output J,
  output JAL,
  output BEQ,
  output BNE,
  output B,
  output I_type_Hazard,
  output [1:0] ALU_o_p,
  output [1:0] extender,
  output Jr,
  output [1:0] immediate,
  output [1:0] R0,
  output [4:0] ALU_function
);

  wire _0, _1, _2, _3, _5, _6, _7, _8, _9, _10, _11, _12, _13, _14, _15, _18, _19, _20, _21, _22, _23, _24,
       _25, _27, _28, _30, _31, ALU0, ALU1, ALU2, ALU3, ALU4, ALU5, ALU6, ALU7, decoder_2_out2, R_type;
  wire [2:2] not_1_out;
  wire [3:0] if_not_R_type, if_R_type;

  Decoder #(.select(5), .enable("false")) decoder_1 (
    .out0(_0), .out1(_1), .out2(_2), .out3(_3), .out4(extender[0]), .out5(_5), .out6(_6), .out7(_7),
    .out8(_8), .out9(_9), .out10(_10), .out11(_11), .out12(_12), .out13(_13), .out14(_14), .out15(_15),
    .out16(MemRead), .out17(MemWrite), .out18(_18), .out19(_19), .out20(_20), .out21(_21), .out22(_22),
    .out23(_23), .out24(_24), .out25(_25), .out26(Jr), .out27(_27), .out28(_28), .out29(R0[1]), .out30(_30),
    .out31(_31), .sel(OpCode));
  or or_1 (R_type, _0, _1);
  or u_ALU_SRC (ALU_SRC, extender[0], _5, _6, _7, _8, _9, _10, _11, _12, _13, MemRead, MemWrite, _28);
  or ALU_O_P2 (ALU_o_p[1], _22, _23, _24, _25);
  nor ALU_O_P1 (ALU_o_p[0], _14, _15, _20, _21, _22, _23);
  or extend2 (extender[1], _8, _9, _10, MemRead, MemWrite, _28);
  or or_2 (immediate[0], _20, _21, _22, _23, _24, _25, Jr, _27, _28, R0[1]);
  or or_3 (immediate[1], _30, _31);
  nor RW (WR, _14, _15, MemWrite, _20, _21, _22, _23, _24, _25, Jr, _30);
  or u_RegDist (RegDist, _14, _15, MemWrite, _20, _21, _22, _23, _24, _25, Jr, _27, R0[1]);
  or R01 (R0[0], _20, _21, _22, _23, _24, _25, Jr, _27, _28);
  or or_4 (TE, _23, _25);
  or or_5 (J, _30, _31);
  or or_6 (JAL, _27, _31);
  or or_7 (BEQ, _14, _20);
  or or_8 (BNE, _15, _21);
  Decoder #(.select(2), .enable("false")) decoder_2 (.out2(decoder_2_out2), .sel({_0, _1}));  // open: out0, out1, out3
  not not_1 (not_1_out[2], decoder_2_out2);
  or or_9 (B, _20, _21, _22, _23, _24, _25, Jr, _27);
  Decoder #(.select(3), .enable("false")) decoder_3 (
    .out0(ALU0), .out1(ALU1), .out2(ALU2), .out3(ALU3), .out4(ALU4), .out5(ALU5), .out6(ALU6), .out7(ALU7),
    .sel({not_1_out[2], R_type_function}));
  or or_10 (I_type_Hazard, extender[0], _5, _6, _7, _8, _9, _10, _11, _12, _13, _14, _15, MemRead, MemWrite);
  or or_11 (if_R_type[3], ALU4, ALU5, ALU6);
  nor nor_1 (if_not_R_type[3], extender[0], _5, _6, _7, _10, _11, _12, _13);
  or or_12 (if_not_R_type[2], _9, _11, _12, _13);
  or or_13 (if_R_type[1], ALU2, ALU3);
  or or_14 (if_not_R_type[1], _6, _7, _13);
  nor nor_2 (if_R_type[0], ALU0, ALU2, ALU4);
  or or_15 (if_not_R_type[0], _5, _7, _9, _10, _12, _14, _15, _20, _21, _22, _23, _24, _25);
  Multiplexer #(.width(5), .enable("false")) multiplexer_1 (
    .in0({_10, if_not_R_type}), .in1({ALU7, if_R_type[3], ALU6, if_R_type[1:0]}), .out(ALU_function),
    .sel(R_type));

  assign MemToReg = MemRead;
  assign SSEt = R0[1];

  // Other names for the same wires on the sheet: _16 = MemRead; _17 = MemWrite; _26 = Jr; _4 = extender[0];
  //   if_not_R_type[4] = _10; if_R_type (some bits) = {ALU7, ALU6}; _29 = R0[1]

  // Notes on the sheet:
  //   ALU-SRC
  //   ALU-o/p
  //   extender
  //   immediate
  //   WR
  //   MemToReg
  //   RegDist
  //   MemRead
  //   MemWrite
  //   R0
  //   R02
  //   SSET
  //   TE
  //   J
  //   Jr
  //   JAL
  //   BEQ
  //   BNE
  //   B
  //   I-type Hazard
  //   ALU-A
  //   ALU-A
  //   ALU-b
  //   ALU-b
  //   ALU-c
  //   ALU-c
  //   ALU-d
  //   ALU-d
  //   ALU-e
  //   ALU-E
endmodule

module main (
  input  [1:0] in_1,
  input  [1:0] R_type_function,
  input  [4:0] in_3,
  output [4:0] out_4
);

  wire _0, _1, ALU0, ALU1, ALU2, ALU3, ALU4, ALU5, ALU6, ALU7;

  control_unit control_unit_1 (
    .OpCode(in_3), .ALU_function(out_4), .R_type_function(in_1));  // open: MemToReg, MemRead, MemWrite, WR, ALU_SRC, RegDist, SSEt, TE, J, JAL, BEQ, BNE, B, ALU_o_p, extender, R0, Jr, immediate, I_type_Hazard
  Decoder #(.select(2)) decoder_1 (.out0(ALU0), .out1(ALU1), .out2(ALU2), .out3(ALU3), .sel(R_type_function), .en(_0));
  Decoder #(.select(2)) decoder_2 (.out0(ALU4), .out1(ALU5), .out2(ALU6), .out3(ALU7), .sel(R_type_function), .en(_1));
endmodule
