// Logisim project Forwarding Unit.circ as structural Verilog: 1 circuit, main circuit Forwarding Unit
module Forwarding_Unit (
  input  [2:0] EX_MEM_Rd,
  input  [2:0] ID_EX_Rs,
  input  [2:0] MEM_WB_Rd,
  input  [2:0] ID_EX_Rt,
  input  MEM_WB_WR,
  input  EX_MEM_WR,
  output [1:0] Forwarding_A,
  output [1:0] Forwarding_B
);

  wire and_5_out, and_6_out, comparator_1_eq, comparator_2_eq, comparator_3_eq, comparator_4_eq;
  wire [1:0] and_1_out, and_3_out;

  Comparator #(.width(3)) comparator_1 (.a(EX_MEM_Rd), .b(ID_EX_Rs), .eq(comparator_1_eq));  // open: gt, lt
  Comparator #(.width(3)) comparator_2 (.a(MEM_WB_Rd), .b(ID_EX_Rs), .eq(comparator_2_eq));  // open: gt, lt
  Comparator #(.width(3)) comparator_3 (.a(EX_MEM_Rd), .b(ID_EX_Rt), .eq(comparator_3_eq));  // open: gt, lt
  Comparator #(.width(3)) comparator_4 (.a(MEM_WB_Rd), .b(ID_EX_Rt), .eq(comparator_4_eq));  // open: gt, lt
  and and_1 (and_1_out[0], EX_MEM_WR, comparator_1_eq);
  and and_2 (and_1_out[1], comparator_2_eq, MEM_WB_WR);
  and and_3 (and_3_out[0], EX_MEM_WR, comparator_3_eq);
  and and_4 (and_3_out[1], comparator_4_eq, MEM_WB_WR);
  Multiplexer #(.width(2), .enable("false")) multiplexer_1 (
    .in0(and_1_out), .in1(2'b01), .out(Forwarding_A), .sel(and_5_out));
  and and_5 (and_5_out, and_1_out[0], and_1_out[1]);
  Multiplexer #(.width(2), .enable("false")) multiplexer_2 (
    .in0(and_3_out), .in1(2'b01), .out(Forwarding_B), .sel(and_6_out));
  and and_6 (and_6_out, and_3_out[0], and_3_out[1]);
endmodule
