// Logisim project Hazard detection unit1.circ as structural Verilog: 1 circuit, main circuit Hazard detection unit
module Hazard_detection_unit (
  input  ID_EX_MemRead,
  input  [2:0] IF_ID_Rs,
  input  [2:0] IF_ID_Rt,
  input  [2:0] ID_Ex_Rd,
  input  [2:0] IF_ID_Rd,
  input  I_type_Hazard,
  input  SSET,
  input  B,
  input  J,
  output out_10,
  output out_11,
  output out_12
);

  wire and_1_out, and_2_out, and_3_out, comparator_1_eq, comparator_2_eq, comparator_3_eq, comparator_4_eq,
       multiplexer_1_out, or_1_out;
  wire [1:1] selectors;

  Comparator #(.width(3)) comparator_1 (.a(ID_Ex_Rd), .b(IF_ID_Rt), .eq(comparator_1_eq));  // open: gt, lt
  Comparator #(.width(3)) comparator_2 (.a(IF_ID_Rs), .b(ID_Ex_Rd), .eq(comparator_2_eq));  // open: gt, lt
  Comparator #(.width(3)) comparator_3 (.a(IF_ID_Rs), .b(ID_Ex_Rd), .eq(comparator_3_eq));  // open: gt, lt
  Comparator #(.width(3)) comparator_4 (.a(IF_ID_Rd), .b(ID_Ex_Rd), .eq(comparator_4_eq));  // open: gt, lt
  or or_1 (or_1_out, comparator_1_eq, comparator_2_eq);
  and and_1 (and_1_out, comparator_3_eq, ID_EX_MemRead);
  and and_2 (and_2_out, comparator_4_eq, ID_EX_MemRead);
  and and_3 (and_3_out, or_1_out, ID_EX_MemRead);
  or or_2 (selectors[1], SSET, B);
  Multiplexer #(.select(2), .enable("false")) multiplexer_1 (
    .in0(and_3_out), .in1(and_1_out), .in2(and_2_out), .out(multiplexer_1_out),
    .sel({selectors[1], I_type_Hazard}));  // open: in3
  Multiplexer #(.enable("false")) multiplexer_2 (.in0(multiplexer_1_out), .in1(1'b0), .out(out_10), .sel(J));

  assign out_11 = out_10;
  assign out_12 = out_10;

  // Other names for the same wires on the sheet: control_Mux = out_10; IF_ID_write = out_10; PC_write = out_10;
  //   selectors[0] = I_type_Hazard
endmodule
