// Logisim project Register File.circ as structural Verilog
module eight_32_bit_register_file (
  input  [2:0] Read_Register1,
  input  [2:0] Read_Register2,
  input  [2:0] Write_Register,
  input  [31:0] Write_Data,
  input  RegWrite,
  input  clock,
  output [31:0] Read_Data1,
  output [31:0] Read_Data2
);

  wire and_1_out, and_2_out, and_3_out, and_4_out, and_5_out, and_6_out, and_7_out, and_8_out,
       decoder_1_out0, decoder_1_out1, decoder_1_out2, decoder_1_out3, decoder_1_out4, decoder_1_out5,
       decoder_1_out6, decoder_1_out7;
  wire [31:0] R0_q, R1_q, R2_q, R3_q, R4_q, R5_q, R6_q, R7_q;

  Decoder #(.select(3), .enable("false")) decoder_1 (
    .out0(decoder_1_out0), .out1(decoder_1_out1), .out2(decoder_1_out2), .out3(decoder_1_out3),
    .out4(decoder_1_out4), .out5(decoder_1_out5), .out6(decoder_1_out6), .out7(decoder_1_out7),
    .sel(Write_Register));
  and and_1 (and_1_out, decoder_1_out0, RegWrite);
  and and_2 (and_2_out, decoder_1_out1, RegWrite);
  and and_3 (and_3_out, decoder_1_out2, RegWrite);
  and and_4 (and_4_out, decoder_1_out3, RegWrite);
  and and_5 (and_5_out, decoder_1_out4, RegWrite);
  and and_6 (and_6_out, decoder_1_out5, RegWrite);
  and and_7 (and_7_out, decoder_1_out6, RegWrite);
  and and_8 (and_8_out, decoder_1_out7, RegWrite);
  Register #(.width(32)) R0 (.D(Write_Data), .en(and_1_out), .Q(R0_q), .clk(clock));  // open: clr
  Register #(.width(32)) R1 (.D(Write_Data), .en(and_2_out), .Q(R1_q), .clk(clock));  // open: clr
  Register #(.width(32)) R2 (.D(Write_Data), .en(and_3_out), .Q(R2_q), .clk(clock));  // open: clr
  Register #(.width(32)) R3 (.D(Write_Data), .en(and_4_out), .Q(R3_q), .clk(clock));  // open: clr
  Register #(.width(32)) R4 (.D(Write_Data), .en(and_5_out), .Q(R4_q), .clk(clock));  // open: clr
  Register #(.width(32)) R5 (.D(Write_Data), .en(and_6_out), .Q(R5_q), .clk(clock));  // open: clr
  Register #(.width(32)) R6 (.D(Write_Data), .en(and_7_out), .Q(R6_q), .clk(clock));  // open: clr
  Register #(.width(32)) R7 (.D(Write_Data), .en(and_8_out), .Q(R7_q), .clk(clock));  // open: clr
  Multiplexer #(.select(3), .width(32), .enable("false")) multiplexer_1 (
    .in0(R0_q), .in1(R1_q), .in2(R2_q), .in3(R3_q), .in4(R4_q), .in5(R5_q), .in6(R6_q), .in7(R7_q),
    .out(Read_Data1), .sel(Read_Register1));
  Multiplexer #(.select(3), .width(32), .enable("false")) multiplexer_2 (
    .in0(R0_q), .in1(R1_q), .in2(R2_q), .in3(R3_q), .in4(R4_q), .in5(R5_q), .in6(R6_q), .in7(R7_q),
    .out(Read_Data2), .sel(Read_Register2));
endmodule
