// Logisim project forward unit(Branch).circ as structural Verilog: 1 circuit, main circuit Forward unit (Branch)
module Forward_unit__Branch (
  input  [2:0] RD_WR,
  input  [2:0] RD_MEM,
  input  [2:0] RD_EX,
  input  [2:0] RD_ID,
  input  [2:0] RS_ID,
  input  BEQ,
  input  BNE,
  input  B,
  output [1:0] forward_D,
  output [1:0] forward_S
);

  wire or_1_out, or_2_out;
  wire [1:0] multiplexer_1_out, multiplexer_3_out;
  wire [2:0] selectors_D, selectors_S;

  Comparator #(.width(3)) comparator_1 (.a(RD_WR), .b(RS_ID), .eq(selectors_S[0]));  // open: gt, lt
  Comparator #(.width(3)) comparator_2 (.a(RD_MEM), .b(RS_ID), .eq(selectors_S[1]));  // open: gt, lt
  Comparator #(.width(3)) comparator_3 (.a(RD_EX), .b(RS_ID), .eq(selectors_S[2]));  // open: gt, lt
  Comparator #(.width(3)) comparator_4 (.a(RD_WR), .b(RD_ID), .eq(selectors_D[0]));  // open: gt, lt
  Comparator #(.width(3)) comparator_5 (.a(RD_MEM), .b(RD_ID), .eq(selectors_D[1]));  // open: gt, lt
  Comparator #(.width(3)) comparator_6 (.a(RD_EX), .b(RD_ID), .eq(selectors_D[2]));  // open: gt, lt
  Multiplexer #(.select(3), .width(2), .enable("false")) multiplexer_1 (
    .in0(2'b00), .in1(2'b01), .in2(2'b10), .in3(2'b10), .in4(2'b11), .in5(2'b11), .in6(2'b11), .in7(2'b11),
    .out(multiplexer_1_out), .sel(selectors_D));
  Multiplexer #(.width(2), .enable("false")) multiplexer_2 (
    .in0(2'b00), .in1(multiplexer_1_out), .out(forward_D), .sel(or_1_out));
  or or_1 (or_1_out, BNE, B, BEQ);
  Multiplexer #(.select(3), .width(2), .enable("false")) multiplexer_3 (
    .in0(2'b00), .in1(2'b01), .in2(2'b10), .in3(2'b10), .in4(2'b11), .in5(2'b11), .in6(2'b11), .in7(2'b11),
    .out(multiplexer_3_out), .sel(selectors_S));
  Multiplexer #(.width(2), .enable("false")) multiplexer_4 (
    .in0(2'b00), .in1(multiplexer_3_out), .out(forward_S), .sel(or_2_out));
  or or_2 (or_2_out, BNE, BEQ);
endmodule
