// Logisim project 8-bit Extender.circ as structural Verilog: 6 circuits, main circuit 8/20-bit Extender
module _8_20_bit_Extender (
  input  SignEx,
  input  [7:0] Imm,
  output [19:0] out_3
);

  and and_1 (out_3[19], SignEx, Imm[7]);

  assign out_3[18:0] = {{11{out_3[19]}}, Imm};
endmodule

module _8_32_bit_Extender (
  input  [7:0] Imm,
  input  in_2,
  output [31:0] out_3
);

  and and_1 (out_3[31], Imm[7], in_2);

  assign out_3[30:0] = {{23{out_3[31]}}, Imm};
endmodule

module _5_20_bit_EXtender (
  input  SignEx,
  input  [4:0] Imm,
  output [19:0] out_3
);

  and and_1 (out_3[19], SignEx, Imm[4]);

  assign out_3[18:0] = {{14{out_3[19]}}, Imm};
endmodule

module _11_20_bit_Extender (
  input  SignEx,
  input  [10:0] Imm,
  output [19:0] out_3
);

  and and_1 (out_3[19], SignEx, Imm[10]);

  assign out_3[18:0] = {{8{out_3[19]}}, Imm};
endmodule

module _5_32_bit_Extender (
  input  [4:0] Imm,
  input  in_2,
  output [31:0] out_3
);

  and and_1 (out_3[31], Imm[4], in_2);

  assign out_3[30:0] = {{26{out_3[31]}}, Imm};
endmodule

module _20_32_bit_Extender (
  input  [19:0] Imm,
  input  in_2,
  output [31:0] out_3
);

  and and_1 (out_3[31], Imm[19], in_2);

  assign out_3[30:0] = {{11{out_3[31]}}, Imm};
endmodule
