// Logisim project Arithmetic Unit.circ as structural Verilog: 2 circuits, main circuit 1-bit Arithmetic Unit
module _1_bit_Arithmetic_Unit (
  input  in_1,
  input  in_2,
  input  in_3,
  input  in_4,
  output result,
  output Cout
);

  wire xor_1_out;

  xor xor_1 (xor_1_out, in_3, in_2);
  Adder #(.width(1)) adder_1 (.a(in_1), .b(xor_1_out), .out(result), .cin(in_4), .cout(Cout));

  // Other names for the same wires on the sheet: a = in_1; b = in_2; Cin = in_4; sub = in_3
endmodule

module _32_bit_Arithmetic_Unit (
  input  Sub,
  input  [31:0] A,
  input  [31:0] B,
  output [31:0] result,
  output Zero_flag,
  output [31:0] equal,
  output great,
  output less_FLag,
  output [31:0] Less,
  output Overflow_flag
);

  wire n1_bit_arithmetic_unit_1_cout, n1_bit_arithmetic_unit_2_cout, n1_bit_arithmetic_unit_3_cout,
       n1_bit_arithmetic_unit_4_cout, n1_bit_arithmetic_unit_5_cout, n1_bit_arithmetic_unit_6_cout,
       n1_bit_arithmetic_unit_7_cout, n1_bit_arithmetic_unit_8_cout, n1_bit_arithmetic_unit_9_cout,
       n1_bit_arithmetic_unit_10_cout, n1_bit_arithmetic_unit_11_cout, n1_bit_arithmetic_unit_12_cout,
       n1_bit_arithmetic_unit_13_cout, n1_bit_arithmetic_unit_14_cout, n1_bit_arithmetic_unit_15_cout,
       n1_bit_arithmetic_unit_16_cout, n1_bit_arithmetic_unit_17_cout, n1_bit_arithmetic_unit_18_cout,
       n1_bit_arithmetic_unit_19_cout, n1_bit_arithmetic_unit_20_cout, n1_bit_arithmetic_unit_21_cout,
       n1_bit_arithmetic_unit_22_cout, n1_bit_arithmetic_unit_23_cout, n1_bit_arithmetic_unit_24_cout,
       n1_bit_arithmetic_unit_25_cout, n1_bit_arithmetic_unit_26_cout, n1_bit_arithmetic_unit_27_cout,
       n1_bit_arithmetic_unit_28_cout, n1_bit_arithmetic_unit_29_cout, n1_bit_arithmetic_unit_30_cout,
       n1_bit_arithmetic_unit_31_cout, n1_bit_arithmetic_unit_32_cout;

  _1_bit_Arithmetic_Unit u_1_bit_arithmetic_unit_1 (
    .in_1(A[0]), .in_2(B[0]), .in_3(Sub), .result(result[0]), .Cout(n1_bit_arithmetic_unit_1_cout), .in_4(Sub));
  _1_bit_Arithmetic_Unit u_1_bit_arithmetic_unit_2 (
    .in_1(A[1]), .in_2(B[1]), .in_3(Sub), .result(result[1]), .Cout(n1_bit_arithmetic_unit_2_cout),
    .in_4(n1_bit_arithmetic_unit_1_cout));
  _1_bit_Arithmetic_Unit u_1_bit_arithmetic_unit_3 (
    .in_1(A[2]), .in_2(B[2]), .in_3(Sub), .result(result[2]), .Cout(n1_bit_arithmetic_unit_3_cout),
    .in_4(n1_bit_arithmetic_unit_2_cout));
  _1_bit_Arithmetic_Unit u_1_bit_arithmetic_unit_4 (
    .in_1(A[3]), .in_2(B[3]), .in_3(Sub), .result(result[3]), .Cout(n1_bit_arithmetic_unit_4_cout),
    .in_4(n1_bit_arithmetic_unit_3_cout));
  _1_bit_Arithmetic_Unit u_1_bit_arithmetic_unit_5 (
    .in_1(A[4]), .in_2(B[4]), .in_3(Sub), .result(result[4]), .Cout(n1_bit_arithmetic_unit_5_cout),
    .in_4(n1_bit_arithmetic_unit_4_cout));
  _1_bit_Arithmetic_Unit u_1_bit_arithmetic_unit_6 (
    .in_1(A[5]), .in_2(B[5]), .in_3(Sub), .result(result[5]), .Cout(n1_bit_arithmetic_unit_6_cout),
    .in_4(n1_bit_arithmetic_unit_5_cout));
  _1_bit_Arithmetic_Unit u_1_bit_arithmetic_unit_7 (
    .in_1(A[6]), .in_2(B[6]), .in_3(Sub), .result(result[6]), .Cout(n1_bit_arithmetic_unit_7_cout),
    .in_4(n1_bit_arithmetic_unit_6_cout));
  _1_bit_Arithmetic_Unit u_1_bit_arithmetic_unit_8 (
    .in_1(A[7]), .in_2(B[7]), .in_3(Sub), .result(result[7]), .Cout(n1_bit_arithmetic_unit_8_cout),
    .in_4(n1_bit_arithmetic_unit_7_cout));
  _1_bit_Arithmetic_Unit u_1_bit_arithmetic_unit_9 (
    .in_1(A[8]), .in_2(B[8]), .in_3(Sub), .result(result[8]), .Cout(n1_bit_arithmetic_unit_9_cout),
    .in_4(n1_bit_arithmetic_unit_8_cout));
  _1_bit_Arithmetic_Unit u_1_bit_arithmetic_unit_10 (
    .in_1(A[9]), .in_2(B[9]), .in_3(Sub), .result(result[9]), .Cout(n1_bit_arithmetic_unit_10_cout),
    .in_4(n1_bit_arithmetic_unit_9_cout));
  _1_bit_Arithmetic_Unit u_1_bit_arithmetic_unit_11 (
    .in_1(A[10]), .in_2(B[10]), .in_3(Sub), .result(result[10]), .Cout(n1_bit_arithmetic_unit_11_cout),
    .in_4(n1_bit_arithmetic_unit_10_cout));
  _1_bit_Arithmetic_Unit u_1_bit_arithmetic_unit_12 (
    .in_1(A[11]), .in_2(B[11]), .in_3(Sub), .result(result[11]), .Cout(n1_bit_arithmetic_unit_12_cout),
    .in_4(n1_bit_arithmetic_unit_11_cout));
  _1_bit_Arithmetic_Unit u_1_bit_arithmetic_unit_13 (
    .in_1(A[12]), .in_2(B[12]), .in_3(Sub), .result(result[12]), .Cout(n1_bit_arithmetic_unit_13_cout),
    .in_4(n1_bit_arithmetic_unit_12_cout));
  _1_bit_Arithmetic_Unit u_1_bit_arithmetic_unit_14 (
    .in_1(A[13]), .in_2(B[13]), .in_3(Sub), .result(result[13]), .Cout(n1_bit_arithmetic_unit_14_cout),
    .in_4(n1_bit_arithmetic_unit_13_cout));
  _1_bit_Arithmetic_Unit u_1_bit_arithmetic_unit_15 (
    .in_1(A[14]), .in_2(B[14]), .in_3(Sub), .result(result[14]), .Cout(n1_bit_arithmetic_unit_15_cout),
    .in_4(n1_bit_arithmetic_unit_14_cout));
  _1_bit_Arithmetic_Unit u_1_bit_arithmetic_unit_16 (
    .in_1(A[15]), .in_2(B[15]), .in_3(Sub), .result(result[15]), .Cout(n1_bit_arithmetic_unit_16_cout),
    .in_4(n1_bit_arithmetic_unit_15_cout));
  _1_bit_Arithmetic_Unit u_1_bit_arithmetic_unit_17 (
    .in_1(A[16]), .in_2(B[16]), .in_3(Sub), .result(result[16]), .Cout(n1_bit_arithmetic_unit_17_cout),
    .in_4(n1_bit_arithmetic_unit_16_cout));
  _1_bit_Arithmetic_Unit u_1_bit_arithmetic_unit_18 (
    .in_1(B[17]), .in_2(A[17]), .in_3(Sub), .result(result[17]), .Cout(n1_bit_arithmetic_unit_18_cout),
    .in_4(n1_bit_arithmetic_unit_17_cout));
  _1_bit_Arithmetic_Unit u_1_bit_arithmetic_unit_19 (
    .in_1(A[18]), .in_2(B[18]), .in_3(Sub), .result(result[18]), .Cout(n1_bit_arithmetic_unit_19_cout),
    .in_4(n1_bit_arithmetic_unit_18_cout));
  _1_bit_Arithmetic_Unit u_1_bit_arithmetic_unit_20 (
    .in_1(A[19]), .in_2(B[19]), .in_3(Sub), .result(result[19]), .Cout(n1_bit_arithmetic_unit_20_cout),
    .in_4(n1_bit_arithmetic_unit_19_cout));
  _1_bit_Arithmetic_Unit u_1_bit_arithmetic_unit_21 (
    .in_1(A[20]), .in_2(B[20]), .in_3(Sub), .result(result[20]), .Cout(n1_bit_arithmetic_unit_21_cout),
    .in_4(n1_bit_arithmetic_unit_20_cout));
  _1_bit_Arithmetic_Unit u_1_bit_arithmetic_unit_22 (
    .in_1(A[21]), .in_2(B[21]), .in_3(Sub), .result(result[21]), .Cout(n1_bit_arithmetic_unit_22_cout),
    .in_4(n1_bit_arithmetic_unit_21_cout));
  _1_bit_Arithmetic_Unit u_1_bit_arithmetic_unit_23 (
    .in_1(A[22]), .in_2(B[22]), .in_3(Sub), .result(result[22]), .Cout(n1_bit_arithmetic_unit_23_cout),
    .in_4(n1_bit_arithmetic_unit_22_cout));
  _1_bit_Arithmetic_Unit u_1_bit_arithmetic_unit_24 (
    .in_1(A[23]), .in_2(B[23]), .in_3(Sub), .result(result[23]), .Cout(n1_bit_arithmetic_unit_24_cout),
    .in_4(n1_bit_arithmetic_unit_23_cout));
  _1_bit_Arithmetic_Unit u_1_bit_arithmetic_unit_25 (
    .in_1(A[24]), .in_2(B[24]), .in_3(Sub), .result(result[24]), .Cout(n1_bit_arithmetic_unit_25_cout),
    .in_4(n1_bit_arithmetic_unit_24_cout));
  _1_bit_Arithmetic_Unit u_1_bit_arithmetic_unit_26 (
    .in_1(A[25]), .in_2(B[25]), .in_3(Sub), .result(result[25]), .Cout(n1_bit_arithmetic_unit_26_cout),
    .in_4(n1_bit_arithmetic_unit_25_cout));
  _1_bit_Arithmetic_Unit u_1_bit_arithmetic_unit_27 (
    .in_1(A[26]), .in_2(B[26]), .in_3(Sub), .result(result[26]), .Cout(n1_bit_arithmetic_unit_27_cout),
    .in_4(n1_bit_arithmetic_unit_26_cout));
  _1_bit_Arithmetic_Unit u_1_bit_arithmetic_unit_28 (
    .in_1(A[27]), .in_2(B[27]), .in_3(Sub), .result(result[27]), .Cout(n1_bit_arithmetic_unit_28_cout),
    .in_4(n1_bit_arithmetic_unit_27_cout));
  _1_bit_Arithmetic_Unit u_1_bit_arithmetic_unit_29 (
    .in_1(A[28]), .in_2(B[28]), .in_3(Sub), .result(result[28]), .Cout(n1_bit_arithmetic_unit_29_cout),
    .in_4(n1_bit_arithmetic_unit_28_cout));
  _1_bit_Arithmetic_Unit u_1_bit_arithmetic_unit_30 (
    .in_1(A[29]), .in_2(B[29]), .in_3(Sub), .result(result[29]), .Cout(n1_bit_arithmetic_unit_30_cout),
    .in_4(n1_bit_arithmetic_unit_29_cout));
  _1_bit_Arithmetic_Unit u_1_bit_arithmetic_unit_31 (
    .in_1(A[30]), .in_2(B[30]), .in_3(Sub), .result(result[30]), .Cout(n1_bit_arithmetic_unit_31_cout),
    .in_4(n1_bit_arithmetic_unit_30_cout));
  _1_bit_Arithmetic_Unit u_1_bit_arithmetic_unit_32 (
    .in_1(A[31]), .in_2(B[31]), .in_3(Sub), .result(Less[0]), .Cout(n1_bit_arithmetic_unit_32_cout),
    .in_4(n1_bit_arithmetic_unit_31_cout));
  xor xor_1 (Overflow_flag, n1_bit_arithmetic_unit_32_cout, n1_bit_arithmetic_unit_31_cout);
  nor nor_1 (equal[0], result[0], result[1], result[2], result[3], result[4], result[5], result[6], result[7], result[8], result[9], result[10], result[11], result[12], result[13], result[14], result[15], result[16], result[17], result[18], result[19], result[20], result[21], result[22], result[23], result[24], result[25], result[26], result[27], result[28], result[29], result[30], Less[0]);
  nor nor_2 (great, equal[0], Less[0]);

  assign equal[31:1] = {31{1'b0}};
  assign Less[31:1] = {31{1'b0}};
  assign less_FLag = Less[0];
  assign result[31] = Less[0];
  assign Zero_flag = equal[0];

  // Other names for the same wires on the sheet: r0 = result[0]; r1 = result[1]; r2 = result[2]; r3 = result[3];
  //   r4 = result[4]; r5 = result[5]; r6 = result[6]; r7 = result[7]; r8 = result[8]; r9 = result[9];
  //   r10 = result[10]; r11 = result[11]; r12 = result[12]; r13 = result[13]; r14 = result[14]; r15 = result[15];
  //   r16 = result[16]; r17 = result[17]; r18 = result[18]; r19 = result[19]; r20 = result[20]; r21 = result[21];
  //   r22 = result[22]; r23 = result[23]; r24 = result[24]; r25 = result[25]; r26 = result[26]; r27 = result[27];
  //   r28 = result[28]; r29 = result[29]; r30 = result[30]; r31 = Less[0]
endmodule
