// Logisim project CPU.circ as structural Verilog: 1 circuit, main circuit CPU
module CPU (
  input  clear,
  input  in_2,
  input  in_3,
  output [15:0] out_4,
  output [19:0] out_5,
  output [10:0] out_6,
  output [31:0] out_7,
  output [2:0] out_8,
  output [31:0] out_9,
  output [1:0] out_10,
  output [4:0] out_11,
  output [4:0] out_12
);

  wire ALuSrc, B, BEQ, BNE, great, J, JAL, JR, less, MemRead, MemTOReg, MemWrite, RegDist, SSET, TE, WR,
       zeroFlag;
  wire [1:0] ALU_O_P, extendType, ImmedaiteType, R0;
  wire [2:0] _3_bit_Rd, _3_bit_Rs, _3_bit_Rt, multiplexer_1_out;
  wire [4:0] _5_bit_imm;
  wire [7:0] _8_bit_imm;
  wire [19:0] _20_bit_AluResult, adder_1_out, PC;
  wire [31:0] extImm, MEM_ALU, multiplexer_4_out, multiplexer_5_out, multiplexer_6_out, multiplexer_7_out,
       multiplexer_8_out, pc_Extended, ram_1_data, RdSh, ReadData1, ReadData2;

  Register #(.width(20)) u_PC (.D(out_5), .Q(PC), .clk(in_3), .clr(in_2));  // open: en
  Extender extender_1 (
    .in_3(out_4[10:0]), .in_4(_8_bit_imm), .in_5(_5_bit_imm), .extend_input(extendType),
    .immediate(ImmedaiteType), .extended_immediate(extImm));
  PC_Programming pc_programming_1 (
    .PC(PC), .IMM(out_4[10:0]), .BNE(BNE), .B(B), .BEQ(BEQ), .JR(JR), .J(J), .JAL(JAL), .RD(ReadData2),
    .greater(great), .less(less), .zeroFlag(zeroFlag), .in_8(ALU_O_P), .TE(TE), .result(out_5));
  Adder #(.width(20)) adder_1 (.a(PC), .b(20'h2), .out(adder_1_out));  // open: cin, cout
  Instruction_Memory instruction_memory_1 (
    .PC(PC), ._11_bit_immediate(out_4[10:0]), ._8_bit_immediate(_8_bit_imm), ._5_bit_immediate(_5_bit_imm),
    ._5_bit_OpCode(out_4[15:11]), ._3_bit_Rd(_3_bit_Rd), ._3_bit_Rs(_3_bit_Rs), ._3_bit_Rt(_3_bit_Rt),
    ._2_bit_R_Func(out_10), .Clear(clear));
  _20_32_bit_Extender u_20_32_bit_extender_1 (.Imm(adder_1_out), .in_2(1'b0), .out_3(pc_Extended));
  control_unit control_unit_1 (
    .MemToReg(MemTOReg), .MemRead(MemRead), .MemWrite(MemWrite), .WR(WR), .ALU_SRC(ALuSrc),
    .RegDist(RegDist), .SSEt(SSET), .TE(TE), .J(J), .JAL(JAL), .BEQ(BEQ), .BNE(BNE), .B(B),
    .ALU_o_p(ALU_O_P), .extender(extendType), .R0(R0), .OpCode(out_4[15:11]), .ALU_function(out_12), .Jr(JR),
    .immediate(ImmedaiteType), .R_type_function(out_10));
  Multiplexer #(.width(3), .enable("false")) multiplexer_1 (
    .in0(_3_bit_Rt), .in1(_3_bit_Rd), .out(multiplexer_1_out), .sel(RegDist));
  Multiplexer #(.width(3), .enable("false")) multiplexer_2 (.in0(_3_bit_Rd), .in1(3'b111), .out(out_8), .sel(JAL));
  Multiplexer #(.width(32), .enable("false")) multiplexer_3 (.in0(MEM_ALU), .in1(pc_Extended), .out(out_9), .sel(JAL));
  eight_32_bit_register_file eight_32_bit_register_file_1 (
    .Read_Register1(_3_bit_Rs), .Read_Register2(multiplexer_1_out), .Write_Register(out_8),
    .Write_Data(out_9), .Read_Data1(ReadData1), .Read_Data2(ReadData2), .RegWrite(WR), .clock(in_3));
  Shifter #(.width(32)) shifter_1 (.in(ReadData2), .\dist (5'b01000), .out(RdSh));
  Multiplexer #(.select(2), .width(32), .enable("false")) multiplexer_4 (
    .in0(ReadData1), .in1({32{1'b0}}), .in2(extImm), .out(multiplexer_4_out), .sel(R0));  // open: in3
  Multiplexer #(.width(32), .enable("false")) multiplexer_5 (
    .in0(ReadData2), .in1(RdSh), .out(multiplexer_5_out), .sel(SSET));
  Multiplexer #(.width(32), .enable("false")) multiplexer_6 (
    .in0(multiplexer_5_out), .in1(extImm), .out(multiplexer_6_out), .sel(ALuSrc));
  Multiplexer #(.width(32), .enable("false")) multiplexer_7 (
    .in0(multiplexer_4_out), .in1(multiplexer_6_out), .out(multiplexer_7_out), .sel(B));
  Multiplexer #(.width(32), .enable("false")) multiplexer_8 (
    .in0(multiplexer_6_out), .in1(multiplexer_4_out), .out(multiplexer_8_out), .sel(B));
  ALU alu_1 (
    .B(multiplexer_8_out), .A(multiplexer_7_out), .greater(great), .less_Flag(less), .Zero(zeroFlag),
    .result(out_7), .in_3(out_12));
  Shifter #(.width(20)) shifter_2 (.in(out_7[19:0]), .\dist (5'b00010), .out(_20_bit_AluResult));
  RAM #(.addrWidth(20), .dataWidth(32), .bus("separate")) ram_1 (
    .addr(_20_bit_AluResult), .din(ReadData2), .data(ram_1_data), .str(MemWrite), .clk(in_3), .ld(MemRead));  // open: sel, clr
  Multiplexer #(.width(32), .enable("false")) multiplexer_9 (
    .in0(out_7), .in1(ram_1_data), .out(MEM_ALU), .sel(MemTOReg));

  assign out_6 = out_4[10:0];
  assign out_11 = out_4[15:11];

  // Other names for the same wires on the sheet: _2_bit_Func[1:0] = out_10; ALUOp[4:0] = out_12;
  //   ALuResult[31:0] = out_7; CLK = in_3; _11_bit_imm[10:0] = out_4[10:0]; _5_bit_OpCode[4:0] = out_4[15:11]
endmodule
