// Logisim project Instruction Memory.circ as structural Verilog: 3 circuits, main circuit Instruction Memory
module Instruction_Memory (
  input  [19:0] PC,
  input  Clear,
  output [10:0] _11_bit_immediate,
  output [7:0] _8_bit_immediate,
  output [4:0] _5_bit_immediate,
  output [4:0] _5_bit_OpCode,
  output [2:0] _3_bit_Rd,
  output [2:0] _3_bit_Rs,
  output [2:0] _3_bit_Rt,
  output [1:0] _2_bit_R_Func
);

  RAM #(.addrWidth(20), .dataWidth(16), .bus("asynch")) ram_1 (
    .addr(PC), .data({_5_bit_OpCode, _3_bit_Rd, _3_bit_Rs, _3_bit_Rt, _2_bit_R_Func}), .ld(1'b1), .clr(Clear));  // open: sel

  assign _5_bit_immediate = {_3_bit_Rt, _2_bit_R_Func};
  assign _8_bit_immediate = {_3_bit_Rs, _3_bit_Rt, _2_bit_R_Func};
  assign _11_bit_immediate = {_3_bit_Rd, _3_bit_Rs, _3_bit_Rt, _2_bit_R_Func};

  // Other names for the same wires on the sheet: _0 = _2_bit_R_Func[0]; _1 = _2_bit_R_Func[1]; _2 = _3_bit_Rt[0];
  //   _3 = _3_bit_Rt[1]; _4 = _3_bit_Rt[2]; _11 = _5_bit_OpCode[0]; _12 = _5_bit_OpCode[1]; _13 = _5_bit_OpCode[2];
  //   _14 = _5_bit_OpCode[3]; _15 = _5_bit_OpCode[4]; _5 = _3_bit_Rs[0]; _6 = _3_bit_Rs[1]; _7 = _3_bit_Rs[2];
  //   _8 = _3_bit_Rd[0]; _9 = _3_bit_Rd[1]; _10 = _3_bit_Rd[2]

  // Notes on the sheet:
  //   Instruction Memory
endmodule

module Extender (
  input  [1:0] extend_input,
  input  [1:0] immediate,
  input  [10:0] in_3,
  input  [7:0] in_4,
  input  [4:0] in_5,
  output [31:0] extended_immediate
);

  wire [31:0] _5_bit_extended, _8_bit_extended, _11_bit_extended, bit_extender_1_out, bit_extender_2_out,
       bit_extender_3_out, bit_extender_4_out, bit_extender_5_out, bit_extender_6_out, bit_extender_7_out,
       bit_extender_8_out, bit_extender_9_out;

  assign bit_extender_1_out = {{24{1'b0}}, in_4};  // Bit_Extender bit_extender_1
  assign bit_extender_2_out = {{24{1'b1}}, in_4};  // Bit_Extender bit_extender_2
  assign bit_extender_3_out = {{24{in_4[7]}}, in_4};  // Bit_Extender bit_extender_3
  assign bit_extender_4_out = {{27{1'b0}}, in_5};  // Bit_Extender bit_extender_4
  assign bit_extender_5_out = {{27{1'b1}}, in_5};  // Bit_Extender bit_extender_5
  assign bit_extender_6_out = {{27{in_5[4]}}, in_5};  // Bit_Extender bit_extender_6
  assign bit_extender_7_out = {{21{1'b0}}, in_3};  // Bit_Extender bit_extender_7
  assign bit_extender_8_out = {{21{1'b1}}, in_3};  // Bit_Extender bit_extender_8
  assign bit_extender_9_out = {{21{in_3[10]}}, in_3};  // Bit_Extender bit_extender_9
  Multiplexer #(.select(2), .width(32), .enable("false")) multiplexer_1 (
    .in0(bit_extender_1_out), .in1(bit_extender_2_out), .in2(bit_extender_3_out), .out(_8_bit_extended),
    .sel(extend_input));  // open: in3
  Multiplexer #(.select(2), .width(32), .enable("false")) multiplexer_2 (
    .in0(bit_extender_4_out), .in1(bit_extender_5_out), .in2(bit_extender_6_out), .out(_5_bit_extended),
    .sel(extend_input));  // open: in3
  Multiplexer #(.select(2), .width(32), .enable("false")) multiplexer_3 (
    .in0(bit_extender_7_out), .in1(bit_extender_8_out), .in2(bit_extender_9_out), .out(_11_bit_extended),
    .sel(extend_input));  // open: in3
  Multiplexer #(.select(2), .width(32), .enable("false")) multiplexer_4 (
    .in0(_5_bit_extended), .in1(_8_bit_extended), .in2(_11_bit_extended), .out(extended_immediate),
    .sel(immediate));  // open: in3

  // Other names for the same wires on the sheet: _5_bit_immediate[4:0] = in_5; _8_bit_immediate[7:0] = in_4;
  //   _11_bit_immediate[10:0] = in_3
endmodule

module main (
);

  Instruction_Memory instruction_memory_1 ();  // open: PC, _11_bit_immediate, _8_bit_immediate, _5_bit_immediate, _5_bit_OpCode, _3_bit_Rd, _3_bit_Rs, _3_bit_Rt, _2_bit_R_Func, Clear
  Extender extender_1 ();  // open: in_3, in_4, in_5, extend_input, immediate, extended_immediate
endmodule
