// Logisim project PC Programming.circ as structural Verilog: 1 circuit, main circuit PC Programming
module PC_Programming (
  input  [19:0] PC,
  input  [10:0] IMM,
  input  [31:0] RD,
  input  BNE,
  input  B,
  input  BEQ,
  input  TE,
  input  [1:0] in_8,
  input  zeroFlag,
  input  less,
  input  greater,
  input  JR,
  input  J,
  input  JAL,
  output [19:0] result
);

  wire and_1_out, and_2_out, and_3_out, and_4_out, and_5_out, and_6_out, and_7_out, and_8_out, and_9_out,
       condition, multiplexer_5_out, not_1_out, not_2_out, not_3_out, not_4_out, not_5_out, not_6_out,
       not_7_out, not_8_out, not_9_out, not_10_out, not_11_out, not_12_out, not_13_out, not_14_out,
       not_15_out, not_16_out, not_17_out, not_18_out, not_19_out, not_20_out, not_21_out, not_22_out,
       not_23_out, not_24_out, not_25_out, not_26_out, not_27_out, not_28_out, not_29_out, not_30_out,
       not_31_out, not_32_out, not_33_out, not_34_out, not_35_out, not_36_out, not_37_out, not_38_out,
       not_39_out, not_40_out, or_1_out, or_2_out, or_3_out, or_4_out;
  wire [7:0] shifter_2_out, shifter_3_out;
  wire [10:0] shifter_1_out;
  wire [19:0] _5_20, _8_20, _8_20_JR, _8_20_shifted_first, _11_20_J, adder_7_out, multiplexer_1_out,
       multiplexer_2_out, multiplexer_3_out, n5_20_bit_extender_1_out_3, n8_20_bit_extender_1_out_3,
       n8_20_bit_extender_2_out_3, n11_20_bit_extender_1_out_3, PC_2, shifter_4_out, shifter_5_out;
  wire [31:0] n8_32_bit_extender_1_out_3;
  wire [31:20] adder_6_out;

  Shifter #(.width(11)) shifter_1 (.in(IMM), .\dist (4'b0001), .out(shifter_1_out));
  Shifter shifter_2 (.in(IMM[7:0]), .\dist (3'b001), .out(shifter_2_out));
  Shifter shifter_3 (.in(IMM[7:0]), .\dist (3'b001), .out(shifter_3_out));
  _5_20_bit_EXtender u_5_20_bit_extender_1 (.SignEx(1'b1), .Imm(IMM[4:0]), .out_3(n5_20_bit_extender_1_out_3));
  _11_20_bit_Extender u_11_20_bit_extender_1 (.SignEx(1'b1), .Imm(shifter_1_out), .out_3(n11_20_bit_extender_1_out_3));
  Shifter #(.width(20)) shifter_4 (.in(n5_20_bit_extender_1_out_3), .\dist (5'b00001), .out(shifter_4_out));
  _8_20_bit_Extender u_8_20_bit_extender_1 (.SignEx(1'b1), .Imm(IMM[7:0]), .out_3(n8_20_bit_extender_1_out_3));
  _8_20_bit_Extender u_8_20_bit_extender_2 (.SignEx(1'b1), .Imm(shifter_2_out), .out_3(n8_20_bit_extender_2_out_3));
  Adder #(.width(20)) adder_1 (.a(PC), .b(n11_20_bit_extender_1_out_3), .out(_11_20_J));  // open: cin, cout
  Adder #(.width(20)) adder_2 (.a(PC_2), .b(shifter_4_out), .out(_5_20));  // open: cin, cout
  _8_32_bit_Extender u_8_32_bit_extender_1 (.Imm(shifter_3_out), .in_2(1'b1), .out_3(n8_32_bit_extender_1_out_3));
  Adder #(.width(20)) adder_3 (.a(PC), .b(20'h2), .out(PC_2));  // open: cin, cout
  Shifter #(.width(20)) shifter_5 (.in(n8_20_bit_extender_1_out_3), .\dist (5'b00001), .out(shifter_5_out));
  Adder #(.width(20)) adder_4 (.a(PC_2), .b(n8_20_bit_extender_2_out_3), .out(_8_20_shifted_first));  // open: cin, cout
  not not_1 (not_1_out, JAL);
  Adder #(.width(20)) adder_5 (.a(PC_2), .b(shifter_5_out), .out(_8_20));  // open: cin, cout
  Adder #(.width(32)) adder_6 (
    .a(n8_32_bit_extender_1_out_3), .b(RD), .out({adder_6_out, _8_20_JR}));  // open: cin, cout
  Adder #(.width(20)) adder_7 (.a(PC), .b(20'h2), .out(adder_7_out));  // open: cin, cout
  and and_1 (and_1_out, condition, not_1_out, BEQ, not_3_out, not_2_out, not_5_out, not_4_out);
  not not_2 (not_2_out, BNE);
  not not_3 (not_3_out, J);
  or or_1 (or_1_out, and_1_out, and_2_out);
  not not_4 (not_4_out, B);
  not not_5 (not_5_out, JR);
  Multiplexer #(.width(20), .enable("false")) multiplexer_1 (
    .in0(adder_7_out), .in1(_5_20), .out(multiplexer_1_out), .sel(or_1_out));
  not not_6 (not_6_out, JAL);
  and and_2 (and_2_out, condition, not_6_out, not_7_out, not_8_out, BNE, not_9_out, not_10_out);
  not not_7 (not_7_out, BEQ);
  not not_8 (not_8_out, J);
  not not_9 (not_9_out, JR);
  not not_10 (not_10_out, B);
  not not_11 (not_11_out, JAL);
  and and_3 (and_3_out, condition, not_11_out, BEQ, not_13_out, not_12_out, not_14_out, B);
  not not_12 (not_12_out, BNE);
  not not_13 (not_13_out, J);
  not not_14 (not_14_out, JR);
  not not_15 (not_15_out, JAL);
  Multiplexer #(.width(20), .enable("false")) multiplexer_2 (
    .in0(multiplexer_1_out), .in1(_8_20), .out(multiplexer_2_out), .sel(or_2_out));
  or or_2 (or_2_out, and_3_out, and_4_out, and_5_out);
  and and_4 (and_4_out, condition, not_15_out, not_17_out, not_18_out, not_16_out, not_19_out, B);
  not not_16 (not_16_out, BNE);
  not not_17 (not_17_out, BEQ);
  not not_18 (not_18_out, J);
  not not_19 (not_19_out, JR);
  not not_20 (not_20_out, JAL);
  and and_5 (and_5_out, condition, not_20_out, not_21_out, not_22_out, BNE, not_23_out, B);
  not not_21 (not_21_out, BEQ);
  not not_22 (not_22_out, J);
  not not_23 (not_23_out, JR);
  not not_24 (not_24_out, JAL);
  Multiplexer #(.width(20), .enable("false")) multiplexer_3 (
    .in0(multiplexer_2_out), .in1(_8_20_JR), .out(multiplexer_3_out), .sel(or_3_out));
  and and_6 (and_6_out, not_24_out, not_26_out, not_27_out, not_25_out, JR, B);
  not not_25 (not_25_out, BNE);
  not not_26 (not_26_out, BEQ);
  not not_27 (not_27_out, J);
  Multiplexer #(.enable("false")) multiplexer_4 (.in0(multiplexer_5_out), .in1(not_28_out), .out(condition), .sel(TE));
  not not_28 (not_28_out, multiplexer_5_out);
  Multiplexer #(.select(2), .enable("false")) multiplexer_5 (
    .in0(zeroFlag), .in2(less), .in3(greater), .out(multiplexer_5_out), .sel(in_8));  // open: in1
  or or_3 (or_3_out, and_6_out, and_7_out);
  not not_29 (not_29_out, BEQ);
  and and_7 (and_7_out, JAL, not_29_out, not_31_out, not_30_out, JR, B);
  not not_30 (not_30_out, BNE);
  not not_31 (not_31_out, J);
  not not_32 (not_32_out, BEQ);
  not not_33 (not_33_out, JAL);
  and and_8 (and_8_out, not_33_out, not_32_out, J, not_34_out, not_36_out, not_35_out);
  not not_34 (not_34_out, BNE);
  Multiplexer #(.width(20), .enable("false")) multiplexer_6 (
    .in0(multiplexer_3_out), .in1(_11_20_J), .out(result), .sel(or_4_out));
  or or_4 (or_4_out, and_8_out, and_9_out);
  not not_35 (not_35_out, B);
  not not_36 (not_36_out, JR);
  not not_37 (not_37_out, BEQ);
  and and_9 (and_9_out, JAL, not_37_out, J, not_38_out, not_39_out, not_40_out);
  not not_38 (not_38_out, BNE);
  not not_39 (not_39_out, JR);
  not not_40 (not_40_out, B);

  // Other names for the same wires on the sheet: A0 = IMM[0]; A1 = IMM[1]; A2 = IMM[2]; A3 = IMM[3]; A4 = IMM[4];
  //   A5 = IMM[5]; A6 = IMM[6]; A7 = IMM[7]; ALU_O_P[1:0] = in_8; A8 = IMM[8]; A9 = IMM[9]; A10 = IMM[10]

  // Notes on the sheet:
  //   BEQ
  //   BNE
  //   BEQZ
  //   BGT/BGTZ/BLT/BLTZ
  //   BNEZ
  //   JR
  //   JAR
  //   J
  //   JAL
endmodule
