// Logisim project test.circ as structural Verilog: 1 circuit, main circuit main
module main (
  input  in_1,
  input  in_2,
  input  in_3,
  input  in_4,
  input  in_5,
  input  in_6,
  input  [19:0] PC,
  input  [31:0] RD,
  input  [10:0] IMM,
  input  [31:0] A,
  input  [31:0] B,
  input  [4:0] in_12,
  output [19:0] out_13,
  output [31:0] out_14
);

  wire alu_1_greater, alu_1_less_flag, alu_1_zero;

  ALU alu_1 (
    .B(B), .A(A), .greater(alu_1_greater), .less_Flag(alu_1_less_flag), .Zero(alu_1_zero), .result(out_14),
    .in_3(in_12));
  // PC_Programming pc_programming_1: pin names not known; wires that end beside it: PC, RD, IMM, in_1, alu_1_zero, in_2, in_3, alu_1_less_flag, in_4, in_5, alu_1_greater, in_6, out_13
endmodule
